// Logisim project cpu.circ as structural Verilog: 7 circuits, main circuit main
module main (
  output [3:0] out_1,
  output [3:0] out_2
);

  wire alu_1_jump, clock_1_out, keyboard_2_clk_out, rom_1_ov;
  wire [3:0] alu_1_alu_out, keyboard_2_user_out, ram_1_ram_out, reg_1_reg_out;
  wire [6:0] keyboard_1_data;
  wire [7:0] reg_1_adr_out, rom_1_rom_out;

  Keyboard_part keyboard_1 (.clk(keyboard_2_clk_out), .data(keyboard_1_data));  // open: re, clr, avail
  LED led_1 (.in(rom_1_ov));
  Keyboard keyboard_2 (
    .befehlsbus(rom_1_rom_out), .keyboard_in(keyboard_1_data), .user_out(keyboard_2_user_out),
    .clk_in(clock_1_out), .clk_out(keyboard_2_clk_out));
  REG reg_1 (
    .befehlsbus(rom_1_rom_out), .a_out(out_1), .d_out(out_2), .clk(clock_1_out), .alu_in(alu_1_alu_out),
    .adr_out(reg_1_adr_out), .reg_out(reg_1_reg_out), .ram_in(ram_1_ram_out), .user_in(keyboard_2_user_out));
  RAM ram_1 (
    .adr_in(reg_1_adr_out), .data_in(reg_1_reg_out), .befehlbus(rom_1_rom_out), .ram_out(ram_1_ram_out),
    .clk(clock_1_out), .a_in(out_1));
  ROM rom_1 (.rom_out(rom_1_rom_out), .ov(rom_1_ov), .clk(clock_1_out), .jump(alu_1_jump), .adr_in(reg_1_adr_out));
  Clock clock_1 (.out(clock_1_out));
  ALU alu_1 (
    .befehlsbus(rom_1_rom_out), .a_in(out_1), .d_in(out_2), .alu_out(alu_1_alu_out), .jump(alu_1_jump),
    .clk(clock_1_out));

  // Notes on the sheet:
  //   ROM
  //   REG
  //   RAM
  //   ALU
endmodule

module ALU_FLAGS (
  input  [7:0] Befehlsbus,
  input  clk,
  input  alu_enable,
  input  [3:0] alu_in,
  input  g,
  input  e,
  input  s,
  input  c_add,
  input  c_inc,
  input  b_sub,
  input  b_dec,
  output jump
);

  wire and_1_out, and_2_out, and_3_out, and_4_out, and_5_out, and_6_out, and_7_out, and_8_out, and_9_out,
       and_10_out, comparator_1_eq, comparator_2_eq, comparator_3_eq, comparator_4_eq, comparator_5_eq,
       comparator_6_eq, comparator_7_eq, comparator_8_eq, comparator_8_gt, d_ff_1_q, d_ff_1_qn, d_ff_2_q,
       d_ff_2_qn, d_ff_3_q, d_ff_3_qn, d_ff_4_q, d_ff_4_qn, d_ff_5_q, d_ff_5_qn, multiplexer_1_out,
       multiplexer_2_out, multiplexer_3_out, multiplexer_4_out, or_1_out, or_2_out;
  wire [2:0] bit_extender_1_out;

  Comparator #(.width(4), .mode("unsigned")) comparator_1 (
    .a(Befehlsbus[7:4]), .b(4'b0111), .eq(comparator_1_eq));  // open: gt, lt
  Comparator #(.width(4), .mode("unsigned")) comparator_2 (
    .a(Befehlsbus[7:4]), .b(4'b0110), .eq(comparator_2_eq));  // open: gt, lt
  Comparator #(.width(4), .mode("unsigned")) comparator_3 (
    .a(Befehlsbus[3:0]), .b(4'b0010), .eq(comparator_3_eq));  // open: gt, lt
  Comparator #(.width(4), .mode("unsigned")) comparator_4 (
    .a(Befehlsbus[3:0]), .b(4'b0000), .eq(comparator_4_eq));  // open: gt, lt
  Comparator #(.width(4), .mode("unsigned")) comparator_5 (
    .a(Befehlsbus[3:0]), .b(4'b0011), .eq(comparator_5_eq));  // open: gt, lt
  Comparator #(.width(4), .mode("unsigned")) comparator_6 (
    .a(Befehlsbus[3:0]), .b(4'b0001), .eq(comparator_6_eq));  // open: gt, lt
  Comparator #(.width(4), .mode("unsigned")) comparator_7 (
    .a(Befehlsbus[3:0]), .b(4'b0100), .eq(comparator_7_eq));  // open: gt, lt
  Comparator #(.width(4), .mode("unsigned")) comparator_8 (
    .a(alu_in), .b(4'b0000), .gt(comparator_8_gt), .eq(comparator_8_eq));  // open: lt
  Multiplexer #(.disabled(0), .enable("false")) multiplexer_1 (
    .in0(comparator_8_gt), .in1(g), .out(multiplexer_1_out), .sel(comparator_7_eq));
  Multiplexer #(.disabled(0), .enable("false")) multiplexer_2 (
    .in0(comparator_8_eq), .in1(e), .out(multiplexer_2_out), .sel(comparator_7_eq));
  and and_1 (and_1_out, comparator_6_eq, b_sub);
  and and_2 (and_2_out, comparator_5_eq, b_dec);
  and and_3 (and_3_out, comparator_4_eq, c_add);
  or or_1 (or_1_out, and_3_out, and_4_out);
  and and_4 (and_4_out, comparator_3_eq, c_inc);
  or or_2 (or_2_out, and_1_out, and_2_out);
  Bit_Extender #(.in_width(4), .out_width(3)) bit_extender_1 (.in(Befehlsbus[3:0]), .out(bit_extender_1_out));
  and and_5 (and_5_out, clk, alu_enable);
  D_Flip_Flop d_ff_1 (.clk(and_5_out), .D(and_6_out), .Q(d_ff_1_q), .Qn(d_ff_1_qn));  // open: preset, en, reset
  and and_6 (and_6_out, alu_enable, multiplexer_1_out);
  D_Flip_Flop d_ff_2 (.clk(and_5_out), .D(and_7_out), .Q(d_ff_2_q), .Qn(d_ff_2_qn));  // open: preset, en, reset
  and and_7 (and_7_out, alu_enable, multiplexer_2_out);
  D_Flip_Flop d_ff_3 (.clk(and_5_out), .D(and_8_out), .Q(d_ff_3_q), .Qn(d_ff_3_qn));  // open: preset, en, reset
  and and_8 (and_8_out, alu_enable, s);
  D_Flip_Flop d_ff_4 (.clk(and_5_out), .D(and_9_out), .Q(d_ff_4_q), .Qn(d_ff_4_qn));  // open: preset, en, reset
  and and_9 (and_9_out, or_1_out, alu_enable);
  D_Flip_Flop d_ff_5 (.clk(and_5_out), .D(and_10_out), .Q(d_ff_5_q), .Qn(d_ff_5_qn));  // open: preset, en, reset
  and and_10 (and_10_out, or_2_out, alu_enable);
  Multiplexer #(.select(3), .disabled(0)) multiplexer_3 (
    .in0(d_ff_1_q), .in1(d_ff_2_q), .in2(d_ff_3_q), .in3(d_ff_4_q), .in4(d_ff_5_q), .out(multiplexer_3_out),
    .sel(bit_extender_1_out), .en(comparator_2_eq));  // open: in5, in6, in7
  or or_3 (jump, multiplexer_3_out, multiplexer_4_out);
  Multiplexer #(.select(3), .disabled(0)) multiplexer_4 (
    .in0(d_ff_1_qn), .in1(d_ff_2_qn), .in2(d_ff_3_qn), .in3(d_ff_4_qn), .in4(d_ff_5_qn),
    .out(multiplexer_4_out), .sel(bit_extender_1_out), .en(comparator_1_eq));  // open: in5, in6, in7

  // Notes on the sheet:
  //   JF
  //   JT
  //   INC
  //   ADD
  //   DEC
  //   SUB
  //   CMP
  //   G
  //   E
  //   S
  //   C
  //   B
endmodule

module ALU (
  input  [7:0] befehlsbus,
  input  [3:0] a_in,
  input  [3:0] d_in,
  input  clk,
  output [3:0] alu_out,
  output jump
);

  wire adder_1_cout, adder_2_cout, comparator_1_eq, comparator_2_eq, comparator_2_gt, comparator_2_lt,
       subtractor_1_bout, subtractor_2_bout;
  wire [3:0] adder_1_out, adder_2_out, and_1_out, controlled_buffer_1_out, controlled_buffer_2_out,
       nand_1_out, nor_1_out, not_1_out, or_1_out, shifter_1_out, shifter_2_out, shifter_3_out, shifter_4_p3,
       subtractor_1_out, subtractor_2_out, xnor_1_out, xor_1_out;

  Comparator #(.width(4), .mode("unsigned")) comparator_1 (
    .a(befehlsbus[7:4]), .b(4'b0101), .eq(comparator_1_eq));  // open: gt, lt
  assign controlled_buffer_1_out = comparator_1_eq ? a_in : 4'bz;  // Controlled_Buffer controlled_buffer_1
  Pull_Resistor pull_resistor_1 (.node(controlled_buffer_1_out));
  assign controlled_buffer_2_out = comparator_1_eq ? d_in : 4'bz;  // Controlled_Buffer controlled_buffer_2
  Pull_Resistor pull_resistor_2 (.node(controlled_buffer_2_out));
  Adder #(.width(4)) adder_1 (
    .a(controlled_buffer_1_out), .b(controlled_buffer_2_out), .out(adder_1_out), .cout(adder_1_cout));  // open: cin
  Subtractor #(.width(4)) subtractor_1 (
    .a(controlled_buffer_1_out), .b(controlled_buffer_2_out), .out(subtractor_1_out), .bout(subtractor_1_bout));  // open: bin
  Adder #(.width(4)) adder_2 (
    .a(controlled_buffer_1_out), .b(4'b0001), .out(adder_2_out), .cout(adder_2_cout));  // open: cin
  Subtractor #(.width(4)) subtractor_2 (
    .a(controlled_buffer_1_out), .b(4'b0001), .out(subtractor_2_out), .bout(subtractor_2_bout));  // open: bin
  Comparator #(.width(4)) comparator_2 (
    .a(controlled_buffer_1_out), .b(controlled_buffer_2_out), .gt(comparator_2_gt), .eq(comparator_2_eq),
    .lt(comparator_2_lt));
  assign not_1_out = ~controlled_buffer_1_out;  // NOT_Gate not_1, 4 bits wide
  assign and_1_out = controlled_buffer_1_out & controlled_buffer_2_out;  // AND_Gate and_1, 4 bits wide
  assign nand_1_out = ~(controlled_buffer_1_out & controlled_buffer_2_out);  // NAND_Gate nand_1, 4 bits wide
  assign or_1_out = controlled_buffer_1_out | controlled_buffer_2_out;  // OR_Gate or_1, 4 bits wide
  assign nor_1_out = ~(controlled_buffer_1_out | controlled_buffer_2_out);  // NOR_Gate nor_1, 4 bits wide
  assign xor_1_out = controlled_buffer_1_out ^ controlled_buffer_2_out;  // XOR_Gate xor_1, 4 bits wide
  assign xnor_1_out = ~(controlled_buffer_1_out ^ controlled_buffer_2_out);  // XNOR_Gate xnor_1, 4 bits wide
  Shifter #(.width(4)) shifter_1 (
    .in(controlled_buffer_1_out), .\dist (controlled_buffer_2_out[1:0]), .out(shifter_1_out));
  Shifter #(.width(4), .shift("lr")) shifter_2 (
    .in(controlled_buffer_1_out), .\dist (controlled_buffer_2_out[1:0]), .out(shifter_2_out));
  Shifter #(.width(4), .shift("rl")) shifter_3 (
    .in(controlled_buffer_1_out), .\dist (controlled_buffer_2_out[1:0]), .out(shifter_3_out));
  // Shifter #(.width(4), .shift("rr")) shifter_4: pin names not known; wires that end beside it: controlled_buffer_1_out, controlled_buffer_2_out[3:2], shifter_4_p3
  Multiplexer #(.select(4), .width(4), .disabled(0)) multiplexer_1 (
    .in0(adder_1_out), .in1(subtractor_1_out), .in2(adder_2_out), .in3(subtractor_2_out), .in4(4'b0000),
    .in5(not_1_out), .in6(and_1_out), .in7(nand_1_out), .in8(or_1_out), .in9(nor_1_out), .in10(xor_1_out),
    .in11(xnor_1_out), .in12(shifter_1_out), .in13(shifter_2_out), .in14(shifter_3_out), .in15(shifter_4_p3),
    .out(alu_out), .sel(befehlsbus[3:0]), .en(comparator_1_eq));
  ALU_FLAGS alu_flags_1 (
    .Befehlsbus(befehlsbus), .clk(clk), .alu_enable(comparator_1_eq), .alu_in(alu_out), .g(comparator_2_gt),
    .e(comparator_2_eq), .s(comparator_2_lt), .c_add(adder_1_cout), .c_inc(adder_2_cout),
    .b_sub(subtractor_1_bout), .b_dec(subtractor_2_bout), .jump(jump));
endmodule

module REG (
  input  [3:0] alu_in,
  input  [3:0] user_in,
  input  [3:0] ram_in,
  input  [7:0] befehlsbus,
  input  clk,
  output [3:0] reg_out,
  output [3:0] a_out,
  output [3:0] d_out,
  output [7:0] adr_out
);

  wire and_1_out, and_2_out, and_3_out, and_4_out, and_5_out, comparator_1_eq, comparator_2_eq,
       comparator_3_eq, comparator_4_eq, comparator_5_eq, comparator_6_eq, comparator_7_eq, comparator_8_eq,
       decoder_1_out0, decoder_1_out1, decoder_1_out2, decoder_1_out3, or_1_out, or_2_out, or_3_out,
       or_4_out, or_5_out, or_6_out, or_8_out, or_9_out;
  wire [3:0] controlled_buffer_1_out, multiplexer_1_out, multiplexer_2_out, or_7_out, or_10_out, or_10_out_2;
  wire [7:0] adder_1_out, controlled_buffer_2_out, controlled_buffer_3_out, subtractor_1_out;

  Comparator #(.width(4), .mode("unsigned")) comparator_1 (
    .a(befehlsbus[3:0]), .b(4'b0100), .eq(comparator_1_eq));  // open: gt, lt
  Comparator #(.width(4), .mode("unsigned")) comparator_2 (
    .a(befehlsbus[7:4]), .b(4'b0001), .eq(comparator_2_eq));  // open: gt, lt
  Comparator #(.width(4), .mode("unsigned")) comparator_3 (
    .a(befehlsbus[7:4]), .b(4'b0010), .eq(comparator_3_eq));  // open: gt, lt
  Comparator #(.width(4), .mode("unsigned")) comparator_4 (
    .a(befehlsbus[7:4]), .b(4'b0101), .eq(comparator_4_eq));  // open: gt, lt
  Comparator #(.width(4), .mode("unsigned")) comparator_5 (
    .a(befehlsbus[7:4]), .b(4'b0011), .eq(comparator_5_eq));  // open: gt, lt
  Comparator #(.width(4), .mode("unsigned")) comparator_6 (
    .a(befehlsbus[7:4]), .b(4'b0100), .eq(comparator_6_eq));  // open: gt, lt
  Comparator #(.width(4), .mode("unsigned")) comparator_7 (
    .a(befehlsbus[7:4]), .b(4'b1001), .eq(comparator_7_eq));  // open: gt, lt
  Comparator #(.width(4), .mode("unsigned")) comparator_8 (
    .a(befehlsbus[7:4]), .b(4'b1010), .eq(comparator_8_eq));  // open: gt, lt
  assign controlled_buffer_1_out = comparator_3_eq ? befehlsbus[3:0] : 4'bz;  // Controlled_Buffer controlled_buffer_1
  Pull_Resistor pull_resistor_1 (.node(controlled_buffer_1_out));
  or or_1 (or_1_out, comparator_6_eq, comparator_2_eq);
  Decoder #(.select(2), .disabled(0)) decoder_1 (
    .out0(decoder_1_out0), .out1(decoder_1_out1), .out2(decoder_1_out2), .out3(decoder_1_out3),
    .sel(befehlsbus[3:2]), .en(or_1_out));
  or or_2 (or_2_out, comparator_5_eq, comparator_2_eq);
  and and_1 (and_1_out, ~comparator_1_eq, comparator_4_eq);  // AND_Gate
  and and_2 (and_2_out, befehlsbus[2], comparator_5_eq);
  and and_3 (and_3_out, befehlsbus[3], comparator_5_eq);
  and and_4 (and_4_out, befehlsbus[0], comparator_6_eq);
  and and_5 (and_5_out, befehlsbus[1], comparator_6_eq);
  or or_3 (or_3_out, or_9_out, decoder_1_out2);
  or or_4 (or_4_out, or_9_out, decoder_1_out3);
  or or_5 (or_5_out, and_2_out, and_4_out);
  or or_6 (or_6_out, and_3_out, and_5_out);
  assign or_7_out = controlled_buffer_1_out | alu_in | user_in | ram_in | reg_out;  // OR_Gate or_7, 4 bits wide
  Register #(.width(4)) a (.D(or_7_out), .en(or_8_out), .Q(a_out), .clk(clk));  // open: clr
  or or_8 (or_8_out, decoder_1_out0, and_1_out, comparator_8_eq, comparator_3_eq, comparator_7_eq);
  Register #(.width(4)) d (.D(or_7_out), .en(decoder_1_out1), .Q(d_out), .clk(clk));  // open: clr
  Multiplexer #(.width(4), .enable("false")) multiplexer_1 (
    .in0(or_7_out), .in1(or_10_out), .out(multiplexer_1_out), .sel(or_9_out));
  Register #(.width(4)) pl (.D(multiplexer_1_out), .en(or_3_out), .Q(adr_out[3:0]), .clk(clk));  // open: clr
  Multiplexer #(.width(4), .enable("false")) multiplexer_2 (
    .in0(or_7_out), .in1(or_10_out_2), .out(multiplexer_2_out), .sel(or_9_out));
  Register #(.width(4)) ph (.D(multiplexer_2_out), .en(or_4_out), .Q(adr_out[7:4]), .clk(clk));  // open: clr
  or or_9 (or_9_out, or_6_out, or_5_out);
  Multiplexer #(.select(2), .width(4), .disabled(0)) multiplexer_3 (
    .in0(a_out), .in1(d_out), .in2(adr_out[3:0]), .in3(adr_out[7:4]), .out(reg_out), .sel(befehlsbus[1:0]),
    .en(or_2_out));
  Adder adder_1 (.a(adr_out), .b(8'h1), .out(adder_1_out));  // open: cin, cout
  Subtractor subtractor_1 (.a(adr_out), .b(8'h1), .out(subtractor_1_out));  // open: bin, bout
  assign controlled_buffer_2_out = or_6_out ? subtractor_1_out : 8'bz;  // Controlled_Buffer controlled_buffer_2
  assign controlled_buffer_3_out = or_5_out ? adder_1_out : 8'bz;  // Controlled_Buffer controlled_buffer_3
  Pull_Resistor pull_resistor_2 (.node(controlled_buffer_3_out));
  assign {or_10_out_2, or_10_out} = controlled_buffer_3_out | controlled_buffer_2_out;  // OR_Gate or_10, 8 bits wide
  Pull_Resistor pull_resistor_3 (.node(controlled_buffer_2_out));

  // Notes on the sheet:
  //   MOV
  //   INA
  //   ALU
  //   STO
  //   LOD
  //   POP
  //   TAK
endmodule

module RAM (
  input  [7:0] adr_in,
  input  [3:0] data_in,
  input  [7:0] befehlbus,
  input  [3:0] a_in,
  input  clk,
  output [3:0] ram_out
);

  wire comparator_1_eq, comparator_2_eq, comparator_3_eq, comparator_4_eq, not_1_out, or_1_out;
  wire [3:0] counter_1_q, pull_resistor_1_node, pull_resistor_2_node;

  Comparator #(.width(4), .mode("unsigned")) comparator_1 (
    .a(befehlbus[7:4]), .b(4'b0011), .eq(comparator_1_eq));  // open: gt, lt
  Comparator #(.width(4), .mode("unsigned")) comparator_2 (
    .a(befehlbus[7:4]), .b(4'b0100), .eq(comparator_2_eq));  // open: gt, lt
  Comparator #(.width(4), .mode("unsigned")) comparator_3 (
    .a(befehlbus[7:4]), .b(4'b1000), .eq(comparator_3_eq));  // open: gt, lt
  Comparator #(.width(4), .mode("unsigned")) comparator_4 (
    .a(befehlbus[7:4]), .b(4'b1001), .eq(comparator_4_eq));  // open: gt, lt
  Pull_Resistor pull_resistor_1 (.node(pull_resistor_1_node));
  RAM_part #(.dataWidth(4), .bus("separate")) ram_1 (
    .addr(adr_in), .din(data_in), .data(pull_resistor_1_node), .str(comparator_1_eq), .clk(clk),
    .ld(comparator_2_eq));  // open: sel, clr
  Counter #(.width(4), .max('hf), .trigger("falling")) counter_1 (
    .load(comparator_4_eq), .count(or_1_out), .Q(counter_1_q), .clk(clk));  // open: D, carry, clr
  or or_1 (or_1_out, comparator_3_eq, comparator_4_eq);
  not not_1 (not_1_out, clk);
  Pull_Resistor pull_resistor_2 (.node(pull_resistor_2_node));
  RAM_part #(.addrWidth(4), .dataWidth(4), .bus("separate")) ram_2 (
    .addr(counter_1_q), .din(a_in), .data(pull_resistor_2_node), .str(comparator_3_eq), .clk(not_1_out),
    .ld(comparator_4_eq));  // open: sel, clr
  assign ram_out = pull_resistor_1_node | pull_resistor_2_node;  // OR_Gate or_2, 4 bits wide

  // Notes on the sheet:
  //   STO
  //   LOD
  //   PUSH
  //   POP
endmodule

module ROM (
  input  [7:0] adr_in,
  input  jump,
  input  clk,
  output [7:0] rom_out,
  output ov
);

  wire not_1_out;
  wire [7:0] counter_1_q;

  Counter #(.ongoal("stay")) counter_1 (
    .load(jump), .D(adr_in), .count(not_1_out), .Q(counter_1_q), .carry(ov), .clk(clk));  // open: clr
  not not_1 (not_1_out, jump);
  ROM_part rom_1 (.addr(counter_1_q), .data(rom_out));  // open: sel

  // Notes on the sheet:
  //   contents of rom_1 (hex, n*v repeats v):
  //   20 80 23 14 2f 51 80 2d 18 21 1c 90 64 20 18 1e 30 90 52 80 20 18 1c 40 80 25 18 90 74 90
endmodule

module Keyboard (
  input  [7:0] befehlsbus,
  input  [6:0] keyboard_in,
  input  clk_in,
  output [3:0] user_out,
  output clk_out
);

  wire comparator_1_eq, comparator_2_eq, comparator_3_eq, comparator_4_eq, comparator_5_eq, comparator_6_eq,
       comparator_7_eq, comparator_8_eq, comparator_9_eq, comparator_10_eq, comparator_11_eq,
       comparator_12_eq, comparator_13_eq, comparator_14_eq, comparator_15_eq, comparator_16_eq,
       comparator_17_eq;
  wire [3:0] controlled_buffer_3_out, controlled_buffer_5_out, controlled_buffer_6_out,
       controlled_buffer_9_out, controlled_buffer_11_out, controlled_buffer_12_out, controlled_buffer_13_out,
       controlled_buffer_14_out, controlled_buffer_17_out, controlled_buffer_18_out, pull_resistor_4_node,
       pull_resistor_7_node, pull_resistor_8_node, pull_resistor_10_node, pull_resistor_15_node,
       pull_resistor_16_node;
  wire [6:0] controlled_buffer_1_out;

  Comparator #(.mode("unsigned")) comparator_1 (.a(befehlsbus), .b(8'ha0), .eq(comparator_1_eq));  // open: gt, lt
  assign controlled_buffer_1_out = comparator_1_eq ? keyboard_in : 7'bz;  // Controlled_Buffer controlled_buffer_1
  Pull_Resistor pull_resistor_1 (.node(controlled_buffer_1_out));
  Pull_Resistor pull_resistor_2 (.node(clk_out));
  assign clk_out = comparator_1_eq ? clk_in : 1'bz;  // Controlled_Buffer controlled_buffer_2
  Comparator #(.width(7), .mode("unsigned")) comparator_2 (
    .a(controlled_buffer_1_out), .b(7'b0110000), .eq(comparator_2_eq));  // open: gt, lt
  assign controlled_buffer_3_out = comparator_2_eq ? 4'b0000 : 4'bz;  // Controlled_Buffer controlled_buffer_3
  Pull_Resistor pull_resistor_3 (.node(controlled_buffer_3_out));
  Comparator #(.width(7), .mode("unsigned")) comparator_3 (
    .a(controlled_buffer_1_out), .b(7'b0110001), .eq(comparator_3_eq));  // open: gt, lt
  Pull_Resistor pull_resistor_4 (.node(pull_resistor_4_node));
  assign pull_resistor_4_node = comparator_3_eq ? 4'b0001 : 4'bz;  // Controlled_Buffer controlled_buffer_4
  Comparator #(.width(7), .mode("unsigned")) comparator_4 (
    .a(controlled_buffer_1_out), .b(7'b0110010), .eq(comparator_4_eq));  // open: gt, lt
  assign controlled_buffer_5_out = comparator_4_eq ? 4'b0010 : 4'bz;  // Controlled_Buffer controlled_buffer_5
  Pull_Resistor pull_resistor_5 (.node(controlled_buffer_5_out));
  Comparator #(.width(7), .mode("unsigned")) comparator_5 (
    .a(controlled_buffer_1_out), .b(7'b0110011), .eq(comparator_5_eq));  // open: gt, lt
  assign controlled_buffer_6_out = comparator_5_eq ? 4'b0011 : 4'bz;  // Controlled_Buffer controlled_buffer_6
  Pull_Resistor pull_resistor_6 (.node(controlled_buffer_6_out));
  Comparator #(.width(7), .mode("unsigned")) comparator_6 (
    .a(controlled_buffer_1_out), .b(7'b0110100), .eq(comparator_6_eq));  // open: gt, lt
  Pull_Resistor pull_resistor_7 (.node(pull_resistor_7_node));
  assign pull_resistor_7_node = comparator_6_eq ? 4'b0100 : 4'bz;  // Controlled_Buffer controlled_buffer_7
  Comparator #(.width(7), .mode("unsigned")) comparator_7 (
    .a(controlled_buffer_1_out), .b(7'b0110101), .eq(comparator_7_eq));  // open: gt, lt
  Pull_Resistor pull_resistor_8 (.node(pull_resistor_8_node));
  assign pull_resistor_8_node = comparator_7_eq ? 4'b0101 : 4'bz;  // Controlled_Buffer controlled_buffer_8
  Comparator #(.width(7), .mode("unsigned")) comparator_8 (
    .a(controlled_buffer_1_out), .b(7'b0110110), .eq(comparator_8_eq));  // open: gt, lt
  assign controlled_buffer_9_out = comparator_8_eq ? 4'b0110 : 4'bz;  // Controlled_Buffer controlled_buffer_9
  Pull_Resistor pull_resistor_9 (.node(controlled_buffer_9_out));
  Comparator #(.width(7), .mode("unsigned")) comparator_9 (
    .a(controlled_buffer_1_out), .b(7'b0110111), .eq(comparator_9_eq));  // open: gt, lt
  Pull_Resistor pull_resistor_10 (.node(pull_resistor_10_node));
  assign pull_resistor_10_node = comparator_9_eq ? 4'b0111 : 4'bz;  // Controlled_Buffer controlled_buffer_10
  Comparator #(.width(7), .mode("unsigned")) comparator_10 (
    .a(controlled_buffer_1_out), .b(7'b0111000), .eq(comparator_10_eq));  // open: gt, lt
  assign controlled_buffer_11_out = comparator_10_eq ? 4'b1000 : 4'bz;  // Controlled_Buffer controlled_buffer_11
  Pull_Resistor pull_resistor_11 (.node(controlled_buffer_11_out));
  Comparator #(.width(7), .mode("unsigned")) comparator_11 (
    .a(controlled_buffer_1_out), .b(7'b0111001), .eq(comparator_11_eq));  // open: gt, lt
  assign controlled_buffer_12_out = comparator_11_eq ? 4'b1001 : 4'bz;  // Controlled_Buffer controlled_buffer_12
  Pull_Resistor pull_resistor_12 (.node(controlled_buffer_12_out));
  Comparator #(.width(7), .mode("unsigned")) comparator_12 (
    .a(controlled_buffer_1_out), .b(7'b1100001), .eq(comparator_12_eq));  // open: gt, lt
  assign controlled_buffer_13_out = comparator_12_eq ? 4'b1010 : 4'bz;  // Controlled_Buffer controlled_buffer_13
  Pull_Resistor pull_resistor_13 (.node(controlled_buffer_13_out));
  Comparator #(.width(7), .mode("unsigned")) comparator_13 (
    .a(controlled_buffer_1_out), .b(7'b1100010), .eq(comparator_13_eq));  // open: gt, lt
  assign controlled_buffer_14_out = comparator_13_eq ? 4'b1011 : 4'bz;  // Controlled_Buffer controlled_buffer_14
  Pull_Resistor pull_resistor_14 (.node(controlled_buffer_14_out));
  Comparator #(.width(7), .mode("unsigned")) comparator_14 (
    .a(controlled_buffer_1_out), .b(7'b1100011), .eq(comparator_14_eq));  // open: gt, lt
  Pull_Resistor pull_resistor_15 (.node(pull_resistor_15_node));
  assign pull_resistor_15_node = comparator_14_eq ? 4'b1100 : 4'bz;  // Controlled_Buffer controlled_buffer_15
  Comparator #(.width(7), .mode("unsigned")) comparator_15 (
    .a(controlled_buffer_1_out), .b(7'b1100100), .eq(comparator_15_eq));  // open: gt, lt
  Pull_Resistor pull_resistor_16 (.node(pull_resistor_16_node));
  assign pull_resistor_16_node = comparator_15_eq ? 4'b1101 : 4'bz;  // Controlled_Buffer controlled_buffer_16
  Comparator #(.width(7), .mode("unsigned")) comparator_16 (
    .a(controlled_buffer_1_out), .b(7'b1100101), .eq(comparator_16_eq));  // open: gt, lt
  assign controlled_buffer_17_out = comparator_16_eq ? 4'b1110 : 4'bz;  // Controlled_Buffer controlled_buffer_17
  Pull_Resistor pull_resistor_17 (.node(controlled_buffer_17_out));
  Comparator #(.width(7), .mode("unsigned")) comparator_17 (
    .a(controlled_buffer_1_out), .b(7'b1100110), .eq(comparator_17_eq));  // open: gt, lt
  assign controlled_buffer_18_out = comparator_17_eq ? 4'b1111 : 4'bz;  // Controlled_Buffer controlled_buffer_18
  Pull_Resistor pull_resistor_18 (.node(controlled_buffer_18_out));
  assign user_out = controlled_buffer_3_out | pull_resistor_4_node | controlled_buffer_5_out | controlled_buffer_6_out | pull_resistor_7_node | pull_resistor_8_node | controlled_buffer_9_out | pull_resistor_10_node | controlled_buffer_11_out | controlled_buffer_12_out | controlled_buffer_13_out | controlled_buffer_14_out | pull_resistor_15_node | pull_resistor_16_node | controlled_buffer_17_out | controlled_buffer_18_out;  // OR_Gate or_1, 4 bits wide
endmodule
