// Logisim project newcpu.circ as structural Verilog: 9 circuits, main circuit main
module main (
);

  wire clock_1_out;
  wire [7:0] rom_1_dbus_out;

  ROM rom_1 (.clk(clock_1_out), .DBus_out(rom_1_dbus_out));  // open: AdrBus_in, jump
  Clock clock_1 (.out(clock_1_out));
  RAM_Stack ram_stack_1 (.DBus_in(rom_1_dbus_out), .clk(clock_1_out));  // open: AdrBus_in, Reg_in, RAM_Stack_out
endmodule

module Register (
  input  [7:0] Key_in,
  input  [7:0] RAM_in,
  input  [7:0] ALU_in,
  input  [7:0] DBus_in,
  input  Clk,
  output [7:0] Reg_out,
  output [7:0] A_out,
  output [7:0] D_out,
  output [7:0] AdrBus_out
);

  wire decoder_1_out0, decoder_1_out1, decoder_1_out2, decoder_1_out3, or_2_out, stw_reg_1_a, stw_reg_1_decd,
       stw_reg_1_e1_2, stw_reg_1_mux, stw_reg_1_reg_self, stw_reg_1_res;
  wire [3:0] controlled_buffer_1_out;
  wire [7:0] bit_erweiterung_1_out_2, or_1_out, pull_resistor_2_node;
  wire [7:4] PH_q, PL_q;

  Stw_Reg stw_reg_1 (
    .DBus_in(DBus_in), .MUX(stw_reg_1_mux), .Reg_self(stw_reg_1_reg_self), .RES(stw_reg_1_res),
    .A(stw_reg_1_a), .Decd(stw_reg_1_decd), .E1_2(stw_reg_1_e1_2));
  assign controlled_buffer_1_out = stw_reg_1_e1_2 ? DBus_in[3:0] : 4'bz;  // Controlled_Buffer controlled_buffer_1
  Bit_Erweiterung bit_erweiterung_1 (.in_1(controlled_buffer_1_out), .out_2(bit_erweiterung_1_out_2));
  Decoder #(.select(2), .disabled(0)) decoder_1 (
    .out0(decoder_1_out0), .out1(decoder_1_out1), .out2(decoder_1_out2), .out3(decoder_1_out3),
    .sel(DBus_in[3:2]), .en(stw_reg_1_decd));
  Pull_Resistor pull_resistor_1 (.node(bit_erweiterung_1_out_2));
  Pull_Resistor pull_resistor_2 (.node(pull_resistor_2_node));
  assign or_1_out = bit_erweiterung_1_out_2 | Key_in | RAM_in | ALU_in | pull_resistor_2_node;  // OR_Gate or_1, 8 bits wide
  or or_2 (or_2_out, stw_reg_1_a, decoder_1_out0);
  assign pull_resistor_2_node = stw_reg_1_reg_self ? Reg_out : 8'bz;  // Controlled_Buffer controlled_buffer_2
  Multiplexer #(.select(2), .width(8), .disabled(0)) multiplexer_1 (
    .in0(A_out), .in1(D_out), .in2({PL_q, AdrBus_out[3:0]}), .in3({PH_q, AdrBus_out[7:4]}), .out(Reg_out),
    .sel(DBus_in[1:0]), .en(stw_reg_1_mux));
  Register_part A (.D(or_1_out), .en(or_2_out), .Q(A_out), .clk(Clk), .clr(stw_reg_1_res));
  Register_part D (.D(or_1_out), .en(decoder_1_out1), .Q(D_out), .clk(Clk), .clr(stw_reg_1_res));
  Register_part PL (.D(or_1_out), .en(decoder_1_out2), .Q({PL_q, AdrBus_out[3:0]}), .clk(Clk), .clr(stw_reg_1_res));
  Register_part PH (.D(or_1_out), .en(decoder_1_out3), .Q({PH_q, AdrBus_out[7:4]}), .clk(Clk), .clr(stw_reg_1_res));

  // Notes on the sheet:
  //   4
  //   8
endmodule

// Reg Stw
module Stw_Reg (
  input  [7:0] DBus_in,
  output MUX,
  output Reg_self,
  output RES,
  output A,
  output Decd,
  output E1_2
);

  wire comparator_1_eq, comparator_2_eq, comparator_3_eq, comparator_4_eq, comparator_5_eq, comparator_6_eq,
       comparator_7_eq, comparator_8_eq, comparator_9_eq, comparator_10_eq;

  Comparator #(.width(4)) comparator_1 (.a(DBus_in[7:4]), .b(4'b0001), .eq(comparator_1_eq));  // open: gt, lt
  assign MUX = comparator_2_eq ? 1'b1 : 1'bz;  // Controlled_Buffer controlled_buffer_1
  Comparator #(.width(4)) comparator_2 (.a(DBus_in[7:4]), .b(4'b0010), .eq(comparator_2_eq));  // open: gt, lt
  Comparator #(.width(4)) comparator_3 (.a(DBus_in[7:4]), .b(4'b0011), .eq(comparator_3_eq));  // open: gt, lt
  assign MUX = comparator_4_eq ? 1'b1 : 1'bz;  // Controlled_Buffer controlled_buffer_2
  Comparator #(.width(4)) comparator_4 (.a(DBus_in[7:4]), .b(4'b0110), .eq(comparator_4_eq));  // open: gt, lt
  Comparator #(.width(4)) comparator_5 (.a(DBus_in[7:4]), .b(4'b0111), .eq(comparator_5_eq));  // open: gt, lt
  assign MUX = comparator_6_eq ? 1'b1 : 1'bz;  // Controlled_Buffer controlled_buffer_3
  Comparator #(.width(4)) comparator_6 (.a(DBus_in[7:4]), .b(4'b1000), .eq(comparator_6_eq));  // open: gt, lt
  Comparator #(.width(4)) comparator_7 (.a(DBus_in[7:4]), .b(4'b1001), .eq(comparator_7_eq));  // open: gt, lt
  assign MUX = comparator_8_eq ? 1'b1 : 1'bz;  // Controlled_Buffer controlled_buffer_4
  Comparator #(.width(4)) comparator_8 (.a(DBus_in[7:4]), .b(4'b1010), .eq(comparator_8_eq));  // open: gt, lt
  Comparator #(.width(4)) comparator_9 (.a(DBus_in[7:4]), .b(4'b1011), .eq(comparator_9_eq));  // open: gt, lt
  Comparator #(.width(4)) comparator_10 (.a(DBus_in[7:4]), .b(4'b1100), .eq(comparator_10_eq));  // open: gt, lt
  Pull_Resistor pull_resistor_1 (.node(MUX));
  assign Reg_self = comparator_2_eq ? 1'b1 : 1'bz;  // Controlled_Buffer controlled_buffer_5
  assign RES = comparator_10_eq ? 1'b1 : 1'bz;  // Controlled_Buffer controlled_buffer_6
  Pull_Resistor pull_resistor_2 (.node(Reg_self));
  Pull_Resistor pull_resistor_3 (.node(RES));
  assign A = comparator_1_eq ? 1'b1 : 1'bz;  // Controlled_Buffer controlled_buffer_7
  assign Decd = comparator_2_eq ? 1'b1 : 1'bz;  // Controlled_Buffer controlled_buffer_8
  assign A = comparator_3_eq ? 1'b1 : 1'bz;  // Controlled_Buffer controlled_buffer_9
  assign Decd = comparator_5_eq ? 1'b1 : 1'bz;  // Controlled_Buffer controlled_buffer_10
  assign Decd = comparator_7_eq ? 1'b1 : 1'bz;  // Controlled_Buffer controlled_buffer_11
  assign Decd = comparator_9_eq ? 1'b1 : 1'bz;  // Controlled_Buffer controlled_buffer_12
  Pull_Resistor pull_resistor_4 (.node(Decd));
  Pull_Resistor pull_resistor_5 (.node(A));
  assign E1_2 = comparator_1_eq ? 1'b1 : 1'bz;  // Controlled_Buffer controlled_buffer_13
  Pull_Resistor pull_resistor_6 (.node(E1_2));

  // Notes on the sheet:
  //   INA
  //   MOV
  //   ALU
  //   PUSH
  //   POP
  //   STO
  //   LOD
  //   PRN
  //   TAK
  //   RES
endmodule

module Bit_Erweiterung (
  input  [3:0] in_1,
  output [7:0] out_2
);

  assign out_2 = {{4{1'b0}}, in_1};  // Bit_Extender bit_extender_1
endmodule

module ROM (
  input  [7:0] AdrBus_in,
  input  jump,
  input  clk,
  output [7:0] DBus_out
);

  wire not_1_out;
  wire [7:0] counter_1_q;

  not not_1 (not_1_out, jump);
  Counter #(.ongoal("stay")) counter_1 (
    .load(jump), .D(AdrBus_in), .count(not_1_out), .Q(counter_1_q), .clk(clk));  // open: carry, clr
  ROM_part rom_1 (.addr(counter_1_q), .data(DBus_out));  // open: sel

  // Notes on the sheet:
  //   contents of rom_1 (hex, n*v repeats v):
  //   0 0 60 60 70 70
endmodule

module RAM_Stack (
  input  [7:0] AdrBus_in,
  input  [7:0] Reg_in,
  input  [7:0] DBus_in,
  input  clk,
  output [7:0] RAM_Stack_out
);

  wire not_1_out, or_1_out, stw_ram_stack_1_ldram, stw_ram_stack_1_ldst, stw_ram_stack_1_storam,
       stw_ram_stack_1_stost;
  wire [3:0] counter_1_q;
  wire [7:0] ram_1_data, ram_2_data;

  Stw_RAM_Stack stw_ram_stack_1 (
    .DBus_in(DBus_in), .LdRAM(stw_ram_stack_1_ldram), .StoRAM(stw_ram_stack_1_storam),
    .LdSt(stw_ram_stack_1_ldst), .StoSt(stw_ram_stack_1_stost));
  Counter #(.width(4), .max('hf), .trigger("falling")) counter_1 (
    .load(stw_ram_stack_1_ldst), .count(or_1_out), .Q(counter_1_q), .clk(clk));  // open: D, carry, clr
  or or_1 (or_1_out, stw_ram_stack_1_stost, stw_ram_stack_1_ldst);
  RAM #(.bus("separate")) ram_1 (
    .addr(AdrBus_in), .din(Reg_in), .data(ram_1_data), .str(stw_ram_stack_1_storam), .clk(clk),
    .ld(stw_ram_stack_1_ldram));  // open: sel, clr
  RAM #(.addrWidth(4), .bus("separate")) ram_2 (
    .addr(counter_1_q), .din(Reg_in), .data(ram_2_data), .str(stw_ram_stack_1_stost), .clk(not_1_out),
    .ld(stw_ram_stack_1_ldst));  // open: sel, clr
  not not_1 (not_1_out, clk);
  Pull_Resistor pull_resistor_1 (.node(ram_1_data));
  assign RAM_Stack_out = ram_1_data | ram_2_data;  // OR_Gate or_2, 8 bits wide
  Pull_Resistor pull_resistor_2 (.node(ram_2_data));
endmodule

// Stw RAM
module Stw_RAM_Stack (
  input  [7:0] DBus_in,
  output LdRAM,
  output StoRAM,
  output LdSt,
  output StoSt
);

  wire comparator_1_eq, comparator_2_eq, comparator_3_eq, comparator_4_eq;

  Comparator #(.width(4), .mode("unsigned")) comparator_1 (
    .a(DBus_in[7:4]), .b(4'b1000), .eq(comparator_1_eq));  // open: gt, lt
  assign LdRAM = comparator_2_eq ? 1'b1 : 1'bz;  // Controlled_Buffer controlled_buffer_1
  Comparator #(.width(4), .mode("unsigned")) comparator_2 (
    .a(DBus_in[7:4]), .b(4'b1001), .eq(comparator_2_eq));  // open: gt, lt
  Comparator #(.width(4), .mode("unsigned")) comparator_3 (
    .a(DBus_in[7:4]), .b(4'b0110), .eq(comparator_3_eq));  // open: gt, lt
  Comparator #(.width(4), .mode("unsigned")) comparator_4 (
    .a(DBus_in[7:4]), .b(4'b0111), .eq(comparator_4_eq));  // open: gt, lt
  Pull_Resistor pull_resistor_1 (.node(LdRAM));
  assign StoRAM = comparator_1_eq ? 1'b1 : 1'bz;  // Controlled_Buffer controlled_buffer_2
  assign LdSt = comparator_4_eq ? 1'b1 : 1'bz;  // Controlled_Buffer controlled_buffer_3
  Pull_Resistor pull_resistor_2 (.node(LdSt));
  Pull_Resistor pull_resistor_3 (.node(StoRAM));
  assign StoSt = comparator_3_eq ? 1'b1 : 1'bz;  // Controlled_Buffer controlled_buffer_4
  Pull_Resistor pull_resistor_4 (.node(StoSt));

  // Notes on the sheet:
  //   STO
  //   LOD
  //   PUSH
  //   POP
endmodule

module ADD_SUB_COMP (
  input  in_1,
  input  in_2,
  input  in_3,
  input  in_4,
  input  in_5,
  input  in_6,
  input  in_7,
  input  in_8,
  input  in_9,
  input  in_10,
  input  in_11,
  input  in_12,
  input  in_13,
  input  in_14,
  input  in_15,
  input  in_16,
  input  in_17,
  output out_18,
  output out_19,
  output out_20,
  output out_21,
  output out_22,
  output out_23,
  output out_24,
  output out_25,
  output out_26,
  output neg,
  output pos,
  output zero
);

  wire and_1_out, and_2_out, and_3_out, and_4_out, and_5_out, and_6_out, and_7_out, and_8_out, and_9_out,
       and_10_out, and_11_out, and_12_out, and_13_out, and_14_out, and_15_out, and_16_out, not_1_out,
       not_2_out, or_1_out, or_2_out, or_3_out, or_4_out, or_5_out, or_6_out, or_7_out, or_8_out, or_9_out,
       or_10_out, or_11_out, or_12_out, or_13_out, or_14_out, or_15_out, xor_2_out, xor_3_out, xor_5_out,
       xor_6_out, xor_8_out, xor_9_out, xor_11_out, xor_12_out, xor_14_out, xor_16_out, xor_17_out,
       xor_19_out, xor_20_out, xor_21_out, xor_23_out, xor_24_out;

  xor xor_1 (out_18, in_1, xor_2_out);
  and and_1 (and_1_out, xor_2_out, in_1);
  xor xor_2 (xor_2_out, in_2, xor_3_out);
  and and_2 (and_2_out, in_2, xor_3_out);
  xor xor_3 (xor_3_out, in_3, in_1);
  or or_1 (or_1_out, out_18, out_19);
  xor xor_4 (out_19, or_2_out, xor_5_out);
  and and_3 (and_3_out, xor_5_out, or_2_out);
  or or_2 (or_2_out, and_1_out, and_2_out);
  xor xor_5 (xor_5_out, in_4, xor_6_out);
  and and_4 (and_4_out, in_4, xor_6_out);
  xor xor_6 (xor_6_out, in_5, in_1);
  or or_3 (or_3_out, or_1_out, out_20);
  xor xor_7 (out_20, or_4_out, xor_8_out);
  or or_4 (or_4_out, and_3_out, and_4_out);
  xor xor_8 (xor_8_out, in_6, xor_9_out);
  xor xor_9 (xor_9_out, in_7, in_1);
  xor xor_10 (out_21, or_5_out, xor_11_out);
  and and_5 (and_5_out, xor_8_out, or_4_out);
  or or_5 (or_5_out, and_5_out, and_6_out);
  xor xor_11 (xor_11_out, in_8, xor_12_out);
  and and_6 (and_6_out, in_6, xor_9_out);
  xor xor_12 (xor_12_out, in_9, in_1);
  or or_6 (or_6_out, or_3_out, out_21);
  xor xor_13 (out_22, or_7_out, xor_14_out);
  and and_7 (and_7_out, xor_11_out, or_5_out);
  or or_7 (or_7_out, and_7_out, and_8_out);
  xor xor_14 (xor_14_out, in_10, xor_17_out);
  and and_8 (and_8_out, in_8, xor_12_out);
  or or_8 (or_8_out, or_6_out, out_22);
  xor xor_15 (out_23, or_9_out, xor_16_out);
  and and_9 (and_9_out, xor_14_out, or_7_out);
  or or_9 (or_9_out, and_9_out, and_10_out);
  xor xor_16 (xor_16_out, in_12, xor_19_out);
  and and_10 (and_10_out, in_10, xor_17_out);
  xor xor_17 (xor_17_out, in_11, in_1);
  or or_10 (or_10_out, or_8_out, out_23);
  xor xor_18 (out_24, or_11_out, xor_20_out);
  and and_11 (and_11_out, xor_16_out, or_9_out);
  or or_11 (or_11_out, and_11_out, and_12_out);
  and and_12 (and_12_out, in_12, xor_19_out);
  xor xor_19 (xor_19_out, in_13, in_1);
  or or_12 (or_12_out, or_10_out, out_24);
  and and_13 (and_13_out, xor_20_out, or_11_out);
  or or_13 (or_13_out, and_13_out, and_14_out);
  xor xor_20 (xor_20_out, in_14, xor_21_out);
  and and_14 (and_14_out, in_14, xor_21_out);
  xor xor_21 (xor_21_out, in_15, in_1);
  or or_14 (or_14_out, or_12_out, out_25);
  xor xor_22 (out_25, or_13_out, xor_23_out);
  and and_15 (and_15_out, xor_23_out, or_13_out);
  xor xor_23 (xor_23_out, in_16, xor_24_out);
  and and_16 (and_16_out, in_16, xor_24_out);
  xor xor_24 (xor_24_out, in_17, in_1);
  and and_17 (neg, not_1_out, in_1);
  and and_18 (out_26, or_15_out, not_2_out);
  not not_1 (not_1_out, or_15_out);
  not not_2 (not_2_out, in_1);
  or or_15 (or_15_out, and_15_out, and_16_out);
  not not_3 (zero, or_14_out);
  not not_4 (pos, neg);
endmodule

module Programmcounter (
  input  clk,
  input  jmp,
  input  [7:0] adr_in,
  output [7:0] adr_out
);

  wire and_1_out, and_2_out, and_3_out, and_4_out, and_5_out, and_6_out, and_7_out, and_8_out, buffer_1_out,
       buffer_2_out, j_k_ff_1_q, j_k_ff_2_q, j_k_ff_3_q, j_k_ff_4_q, j_k_ff_5_q, j_k_ff_6_q, j_k_ff_7_q,
       not_1_out, not_2_out, not_3_out, not_4_out, not_5_out, not_6_out, not_7_out, not_8_out, not_9_out,
       not_10_out, not_11_out, not_12_out, not_13_out, not_14_out, not_15_out, not_16_out, not_17_out,
       not_18_out, or_1_out, or_2_out, or_3_out, or_4_out, or_5_out, or_6_out, or_7_out, or_8_out, or_9_out,
       or_10_out, or_11_out, or_12_out, or_13_out, or_14_out, or_15_out, or_16_out, or_17_out, or_18_out,
       or_19_out, or_20_out, or_21_out, or_22_out, or_23_out, or_24_out;

  not not_1 (not_1_out, jmp);
  and and_1 (and_1_out, not_2_out, clk);
  not not_2 (not_2_out, not_1_out);
  buf buffer_1 (buffer_1_out, not_1_out);
  or or_1 (or_1_out, and_1_out, clk);
  or or_2 (or_2_out, not_4_out, buffer_2_out);
  or or_3 (or_3_out, not_3_out, buffer_2_out);
  buf buffer_2 (buffer_2_out, buffer_1_out);
  not not_3 (not_3_out, not_4_out);
  not not_4 (not_4_out, adr_in[0]);
  J_K_Flip_Flop j_k_ff_1 (
    .J(or_2_out), .clk(or_1_out), .K(or_3_out), .Q(j_k_ff_1_q), .Qn(adr_out[0]));  // open: preset, en, reset
  or or_4 (or_4_out, and_1_out, and_2_out);
  and and_2 (and_2_out, not_1_out, j_k_ff_1_q);
  or or_5 (or_5_out, not_6_out, buffer_2_out);
  or or_6 (or_6_out, not_5_out, buffer_2_out);
  not not_5 (not_5_out, not_6_out);
  not not_6 (not_6_out, adr_in[1]);
  J_K_Flip_Flop j_k_ff_2 (
    .J(or_5_out), .clk(or_4_out), .K(or_6_out), .Q(j_k_ff_2_q), .Qn(adr_out[1]));  // open: preset, en, reset
  or or_7 (or_7_out, and_1_out, and_3_out);
  and and_3 (and_3_out, not_1_out, j_k_ff_2_q);
  or or_8 (or_8_out, not_7_out, buffer_2_out);
  or or_9 (or_9_out, not_8_out, buffer_2_out);
  not not_7 (not_7_out, not_8_out);
  not not_8 (not_8_out, adr_in[2]);
  and and_4 (and_4_out, not_1_out, j_k_ff_3_q);
  J_K_Flip_Flop j_k_ff_3 (
    .J(or_9_out), .clk(or_7_out), .K(or_8_out), .Q(j_k_ff_3_q), .Qn(adr_out[2]));  // open: preset, en, reset
  or or_10 (or_10_out, and_1_out, and_4_out);
  or or_11 (or_11_out, not_10_out, buffer_2_out);
  or or_12 (or_12_out, not_9_out, buffer_2_out);
  not not_9 (not_9_out, not_10_out);
  not not_10 (not_10_out, adr_in[3]);
  and and_5 (and_5_out, not_1_out, j_k_ff_4_q);
  J_K_Flip_Flop j_k_ff_4 (
    .J(or_11_out), .clk(or_10_out), .K(or_12_out), .Q(j_k_ff_4_q), .Qn(adr_out[3]));  // open: preset, en, reset
  not not_11 (not_11_out, adr_in[4]);
  or or_13 (or_13_out, and_1_out, and_5_out);
  or or_14 (or_14_out, not_11_out, buffer_2_out);
  or or_15 (or_15_out, not_12_out, buffer_2_out);
  not not_12 (not_12_out, not_11_out);
  and and_6 (and_6_out, not_1_out, j_k_ff_5_q);
  J_K_Flip_Flop j_k_ff_5 (
    .J(or_14_out), .clk(or_13_out), .K(or_15_out), .Q(j_k_ff_5_q), .Qn(adr_out[4]));  // open: preset, en, reset
  or or_16 (or_16_out, not_13_out, buffer_2_out);
  not not_13 (not_13_out, adr_in[5]);
  or or_17 (or_17_out, and_1_out, and_6_out);
  J_K_Flip_Flop j_k_ff_6 (
    .J(or_16_out), .clk(or_17_out), .K(or_18_out), .Q(j_k_ff_6_q), .Qn(adr_out[5]));  // open: preset, en, reset
  or or_18 (or_18_out, not_14_out, buffer_2_out);
  not not_14 (not_14_out, not_13_out);
  and and_7 (and_7_out, not_1_out, j_k_ff_6_q);
  or or_19 (or_19_out, not_15_out, buffer_2_out);
  not not_15 (not_15_out, adr_in[6]);
  or or_20 (or_20_out, and_1_out, and_7_out);
  J_K_Flip_Flop j_k_ff_7 (
    .J(or_19_out), .clk(or_20_out), .K(or_21_out), .Q(j_k_ff_7_q), .Qn(adr_out[6]));  // open: preset, en, reset
  or or_21 (or_21_out, not_16_out, buffer_2_out);
  not not_16 (not_16_out, not_15_out);
  or or_22 (or_22_out, and_1_out, and_8_out);
  and and_8 (and_8_out, not_1_out, j_k_ff_7_q);
  or or_23 (or_23_out, not_18_out, buffer_2_out);
  not not_17 (not_17_out, not_18_out);
  not not_18 (not_18_out, adr_in[7]);
  J_K_Flip_Flop j_k_ff_8 (
    .J(or_23_out), .clk(or_22_out), .K(or_24_out), .Qn(adr_out[7]));  // open: Q, preset, en, reset
  or or_24 (or_24_out, not_17_out, buffer_2_out);
endmodule
